# Fritzing sketch Color detection (saved by Fritzing 0.9.2b)

parts:
  e-radionica1 = TCS230 Color Sensor [part_number=101209]
  Componente1 = Arduino Nano (Rev3.0) (ICSP)
  U1 = LCD-16X2 [package=lcd-16x2_nosilk]
  S1 = Pushbutton [package="[THT]"]
  S2 = Pushbutton [package="[THT]"]

nets:
  GND: e-radionica1.Gnd, Componente1.GND, U1.VSS, U1.R_W
  N1: e-radionica1.OE, Componente1.D8
  5V: e-radionica1.S0, Componente1.5V, U1.VDD, U1.A
  N2: e-radionica1.S3, Componente1.D13/SCK
  N3: e-radionica1.S2, Componente1.D12/MISO
  N4: e-radionica1.Out, Componente1.D5
  N5: Componente1.D1/TX, U1.RS
  N6: Componente1.D2, S2.Pin_2
  N7: Componente1.D3, S1.Pin_2
  N8: Componente1.D4, U1.E
  N9: Componente1.D6, U1.DB4
  N10: Componente1.D7, U1.DB5
  N11: Componente1.D9, U1.DB6
  N12: Componente1.D10, U1.DB7
  N13: Componente1.D11/MOSI, U1.VO

custom parts:
  TCS230 Color Sensor: TCS230
